// Digital circuit 2s-complement_4bits.dig as structural Verilog
module _2s_complement_4bits (
  input  A0,
  input  A1,
  input  A2,
  input  A3,
  output S0,
  output S1,
  output S2,
  output S3
);

  wire not_1_out, not_2_out, not_3_out, not_4_out;

  not not_1 (not_1_out, A3);
  not not_2 (not_2_out, A2);
  not not_3 (not_3_out, A1);
  full_adder_4bits_2_c_1 full_adder_4bits_2_c_1_1 (
    .A3(not_1_out), .A2(not_2_out), .A1(not_3_out), .A0(not_4_out), .B0(1'b1), .B1(1'b0), .B2(1'b0),
    .B3(1'b0), .CIN(1'b0), .S0(S0), .S1(S1), .S2(S2), .S3(S3));  // open: Cout
  not not_4 (not_4_out, A0);
endmodule
