// Digital circuit circuit_1(1.3).dig as structural Verilog
module circuit_1_1_3 (
  input  A,
  input  B,
  output S
);

  wire and_1_out, and_2_out, not_1_out, not_2_out;

  not not_1 (not_1_out, A);
  not not_2 (not_2_out, B);
  and and_1 (and_1_out, A, not_2_out);
  and and_2 (and_2_out, not_1_out, B);
  or or_1 (S, and_1_out, and_2_out);
endmodule
