// Digital circuit full-adder_1bit (2.b.1).dig as structural Verilog
module full_adder_1bit__2_b_1 (
  input  A0,
  input  B0,
  input  Cin,
  output S,
  output Cout
);

  wire and_1_out, and_2_out, xor_1_out;

  xor xor_1 (xor_1_out, A0, B0);
  xor xor_2 (S, xor_1_out, Cin);
  and and_1 (and_1_out, A0, B0);
  and and_2 (and_2_out, xor_1_out, Cin);
  or or_1 (Cout, and_1_out, and_2_out);
endmodule

/* Test case tdv:
Cin A0 B0 S Cout
0 0 0 0 0
0 0 1 1 0
0 1 0 1 0
0 1 1 0 1
1 0 0 1 0
1 0 1 0 1
1 1 0 0 1
1 1 1 1 1 
*/
