// Digital circuit full-adder_4bits(2.c.1).dig as structural Verilog
module full_adder_4bits_2_c_1 (
  input  A3,
  input  A2,
  input  A1,
  input  A0,
  input  B0,
  input  B1,
  input  B2,
  input  B3,
  input  CIN,
  output S0,
  output S1,
  output S2,
  output S3,
  output Cout
);

  wire full_adder_1bit__2_b_1_2_cout, full_adder_1bit__2_b_1_3_cout, full_adder_1bit__2_b_1_4_cout;

  full_adder_1bit__2_b_1 full_adder_1bit__2_b_1_1 (
    .A0(A3), .B0(B3), .Cin(full_adder_1bit__2_b_1_2_cout), .S(S3), .Cout(Cout));
  full_adder_1bit__2_b_1 full_adder_1bit__2_b_1_2 (
    .A0(A2), .B0(B2), .Cin(full_adder_1bit__2_b_1_3_cout), .S(S2), .Cout(full_adder_1bit__2_b_1_2_cout));
  full_adder_1bit__2_b_1 full_adder_1bit__2_b_1_3 (
    .A0(A1), .B0(B1), .Cin(full_adder_1bit__2_b_1_4_cout), .S(S1), .Cout(full_adder_1bit__2_b_1_3_cout));
  full_adder_1bit__2_b_1 full_adder_1bit__2_b_1_4 (
    .A0(A0), .B0(B0), .Cin(CIN), .S(S0), .Cout(full_adder_1bit__2_b_1_4_cout));
endmodule

/* Test case script:
CIN A3 A2 A1 A0 B3 B2 B1 B0 Cout S3 S2 S1 S0
loop(A,16)
 loop(B,16)
 0 bits(4,A) bits(4,B) bits(5,A+B)
 1 bits(4,A) bits(4,B) bits(5,A+B+1)
 end loop
end loop
*/
