// Digital circuit half-adder_1bit (2.a.1).dig as structural Verilog
module half_adder_1bit__2_a_1 (
  input  A0,
  input  B0,
  output Cout,
  output S
);

  _1_2 _1_2_1 (.A(A0), .B(B0), .S(S));
  and and_1 (Cout, A0, B0);
endmodule
